# Fritzing sketch Safe_Project (saved by Fritzing 0.9.3b)
breadboards: 3

parts:
  Part1 = PocketBeagle
  R1 = Rotary Potentiometer (Small) [maximum_resistance=100kΩ package=THT]
  R2 = Rotary Potentiometer (Small) [maximum_resistance=100kΩ package=THT]
  R3 = Rotary Potentiometer (Small) [maximum_resistance=100kΩ package=THT]
  S1 = Pushbutton [package="[SMD]"]
  LED1 = smd LED [color="Green (565nm)" package="1206 [SMD]"]
  LED2 = smd LED [color="Red (635nm)" package="1206 [SMD]"]
  S2 = Pushbutton [package="[SMD]"]
  S3 = Pushbutton [package="[SMD]"]
  S4 = Pushbutton [package="[SMD]"]
  S5 = Pushbutton [package="[SMD]"]
  S6 = Pushbutton [package="[SMD]"]
  S7 = Pushbutton [package="[SMD]"]
  S8 = Pushbutton [package="[SMD]"]
  S9 = Pushbutton [package="[SMD]"]
  S10 = Pushbutton [package="[SMD]"]
  S11 = Pushbutton [package="[SMD]"]
  S12 = Pushbutton [package="[SMD]"]
  S13 = Pushbutton [package="[SMD]"]
  S14 = Pushbutton [package="[SMD]"]
  S15 = Pushbutton [package="[SMD]"]
  S16 = Pushbutton [package="[SMD]"]
  S17 = Pushbutton [package="[SMD]"]
  R4 = Resistor [tolerance=±5% resistance=1k package="0402 [SMD]"]
  R5 = Resistor [tolerance=±5% resistance=1k package="0402 [SMD]"]
  R6 = Resistor [tolerance=±5% resistance=1k package="0402 [SMD]"]
  R7 = Resistor [tolerance=±5% resistance=1k package="0402 [SMD]"]
  R8 = Resistor [tolerance=±5% resistance=1k package="0402 [SMD]"]
  R9 = Resistor [tolerance=±5% resistance=1k package="0402 [SMD]"]
  R10 = Resistor [tolerance=±5% resistance=1k package="0402 [SMD]"]
  R11 = Resistor [tolerance=±5% resistance=1k package="0402 [SMD]"]
  R12 = Resistor [tolerance=±5% resistance=1k package="0402 [SMD]"]
  R13 = Resistor [tolerance=±5% resistance=1k package="0402 [SMD]"]
  R14 = Resistor [tolerance=±5% resistance=1k package="0402 [SMD]"]
  R15 = Resistor [tolerance=±5% resistance=1k package="0402 [SMD]"]
  R16 = Resistor [tolerance=±5% resistance=1k package="0402 [SMD]"]
  R17 = Resistor [tolerance=±5% resistance=1k package="0402 [SMD]"]
  R18 = Resistor [tolerance=±5% resistance=1k package="0402 [SMD]"]
  R19 = Resistor [tolerance=±5% resistance=1k package="0402 [SMD]"]
  R20 = Resistor [tolerance=±5% resistance=1k package="0402 [SMD]"]
  LED3 = smd LED [color="Green (565nm)" package="1206 [SMD]"]
  LED4 = smd LED [color="Green (565nm)" package="1206 [SMD]"]
  LED5 = smd LED [color="Red (635nm)" package="1206 [SMD]"]
  LED6 = smd LED [color="Red (635nm)" package="1206 [SMD]"]

nets:
  N1: Part1.AIN.VREFN, Part1.AIN.VREFP, R1.leg1, R1.leg2, R2.leg1, R2.leg2, R3.leg1, R3.leg2, S1.Pin_1, S1.Pin_2, LED1.anode, LED2.anode, S2.Pin_3, S2.Pin_4, S3.Pin_3, S3.Pin_4, S4.Pin_3, S4.Pin_4, S5.Pin_3, S5.Pin_4, S6.Pin_1, S6.Pin_2, S7.Pin_1, S7.Pin_2, S8.Pin_1, S8.Pin_2, S9.Pin_1, S9.Pin_2, S10.Pin_1, S10.Pin_2, S11.Pin_1, S11.Pin_2, S12.Pin_1, S12.Pin_2, S13.Pin_1, S13.Pin_2, S14.Pin_1, S14.Pin_2, S15.Pin_1, S15.Pin_2, S16.Pin_1, S16.Pin_2, S17.Pin_1, S17.Pin_2, R4.Pin_1, R5.Pin_1, R6.Pin_1, R7.Pin_1, R8.Pin_1, R9.Pin_1, R10.Pin_1, R11.Pin_1, R12.Pin_1, R13.Pin_1, R14.Pin_1, R15.Pin_1, R16.Pin_0, R17.Pin_0, R18.Pin_0, R19.Pin_0, R20.Pin_0, LED3.anode, LED4.anode, LED5.anode, LED6.anode
  N2: Part1.AIN0(1.8V), R1.wiper
  N3: Part1.GPIO23, S2.Pin_1, S2.Pin_2, R19.Pin_1
  N4: Part1.GPIO60, LED6.cathode
  N5: Part1.GPIO52, LED4.cathode
  N6: Part1.GPIO47, S17.Pin_3, S17.Pin_4, R13.Pin_0
  N7: S1.Pin_3, S1.Pin_4, R20.Pin_1
  N8: S3.Pin_1, S3.Pin_2, R18.Pin_1
  N9: S4.Pin_1, S4.Pin_2, R17.Pin_1
  N10: S5.Pin_1, S5.Pin_2, R16.Pin_1
  N11: S6.Pin_3, S6.Pin_4, S10.Pin_3, S10.Pin_4, R7.Pin_0, R15.Pin_0
  N12: S7.Pin_3, S7.Pin_4, S11.Pin_3, S11.Pin_4, R4.Pin_0, R8.Pin_0
  N13: S8.Pin_3, S8.Pin_4, S12.Pin_3, S12.Pin_4, R5.Pin_0, R9.Pin_0
  N14: S9.Pin_3, S9.Pin_4, S13.Pin_3, S13.Pin_4, R6.Pin_0, R10.Pin_0
  N15: S14.Pin_3, S14.Pin_4, R11.Pin_0
  N16: S15.Pin_3, S15.Pin_4, R12.Pin_0
  N17: S16.Pin_3, S16.Pin_4, R14.Pin_0
